# Fritzing sketch (fred) protoboard (with touch and vib motor) (saved by Fritzing 1.0.1rc)
breadboards: 1

parts:
  Left_FOOT = Basic Servo
  Componente1 = Arduino Uno (Rev3) - ICSP
  Componente3 = 16 NeoPixel Ring [part_number=1463]
  M1 = MAX7219 8x8 single Led Matrix Module
  V1 = DC Power [voltage=5]  # not connected
  Right_LEG = Basic Servo
  Right_FOOT = Basic Servo
  M2 = MAX7219 8x8 single Led Matrix Module
  M3 = MAX7219 8x8 single Led Matrix Module
  Left_LEG = Basic Servo
  aaaaa = Battery block 9V  # not connected
  U1 = NodeMCU V1.0
  TTP223 = TTP223B Capacitive Touch Sensor Module
  TTP223_2 = TTP223B Capacitive Touch Sensor Module
  TTP223_3 = TTP223B Capacitive Touch Sensor Module
  U2 = Vibration Motor- ROB-08449 [package=vibe-motor-10mm]

nets:
  GND: Left_FOOT.gnd, Componente1.GND, Componente3.GND, M1.I-GND, M1.O-GND, Right_LEG.gnd, Right_FOOT.gnd, M2.I-GND, M2.O-GND, M3.I-GND, M3.O-GND, Left_LEG.gnd, U1.GND
  VCC: Left_FOOT.vcc, Componente3.VDD, M1.I-VCC, M1.O-VCC, Right_LEG.vcc, Right_FOOT.vcc, M2.I-VCC, M2.O-VCC, M3.I-VCC, Left_LEG.vcc
  N1: Left_FOOT.pulse, Componente1.D3_PWM
  N2: Componente1.ICSP_MISO, Componente1.D12/MISO, M1.I-DIN
  N3: Componente1.D8, TTP223_2.SIG
  N4: Componente1.D9_PWM, TTP223_3.SIG
  N5: Componente1.D10_PWM/SS, M1.I-CS, M1.O-CS, M2.I-CS, M2.O-CS, M3.I-CS, M3.O-CS
  N6: Componente1.D11_PWM/MOSI, M1.I-CLK, M1.O-CLK, M2.I-CLK, M2.O-CLK, M3.I-CLK, M3.O-CLK
  N7: Componente1.D13/SCK, U2.-
  N8: Componente1.D0/RX, U1.D2
  N9: Componente1.D1/TX, U1.D3
  N10: Componente1.D2, Left_LEG.pulse
  N11: Componente1.D4, Right_LEG.pulse
  N12: Componente1.D5_PWM, Right_FOOT.pulse
  N13: Componente1.D6_PWM, Componente3.IN
  N14: Componente1.D7, TTP223.SIG
  N15: M1.O-DOUT, M2.I-DIN
  N16: M2.O-DOUT, M3.I-DIN

notes:
  Head
  Sensor
  Left (Ear)
  Sensor
  Right (Ear)
  Sensor
  Right Eye
  Left Eye
  Mouth
  * This battery represents a 5V 2A power supply
  Head
  Vib. Motor

custom parts:
  16 NeoPixel Ring: 16 ultra bright smart LED NeoPixels are arranged in a circle with 1.75" (44.5mm) outer diameter. The rings are 'chainable' - connect the output pin of one to the input pin of another. Use only one microcontroller pin to control as many as you can chain together! Each LED is addressable as the driver chip is inside the LED. Each one has ~18mA constant current drive so the color will be very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
  MAX7219 8x8 single Led Matrix Module: Description: MAX7219 8x8 LedMatrix single Red Module Dimensions: 32x32mm Documents:
  NodeMCU V1.0: ESP8266 based NodeMCU
  TTP223B Capacitive Touch Sensor Module: The TTP223B capacitive touch sensor module uses the TTP223B IC. The appropriate voltage is approximately 2 to 5.5 volts.
